// Logisim project rv32_all.circ as structural Verilog: 3 circuits, main circuit main
module main (
  output out_1,
  output [31:0] out_2,
  output [31:0] out_3,
  output [31:0] out_4,
  output [31:0] out_5,
  output [31:0] out_6,
  output [31:0] out_7,
  output [31:0] out_8,
  output [31:0] out_9,
  output [31:0] out_10,
  output [31:0] out_11,
  output [31:0] out_12
);

  wire blt, br_eq, clk, ld_en, rf_we, sw_en;
  wire [1:0] op2_sel, pc_sel;
  wire [2:0] alu_fun, wb_sel;
  wire [4:0] inst_decoder_1_rd, inst_decoder_1_rs1, inst_decoder_1_rs2;
  wire [31:0] alu_1_alu_out, auipc_result, branch_target, data_ram_dout, i_im, inst_mem_data, j_im,
       jal_target, jalr_sum, jalr_target, multiplexer_1_out, multiplexer_2_out, multiplexer_3_out, pc_plus4,
       pc_q, rf32_1_rd1, rf32_1_rd2, s_im, sb_im, u_im;

  Clock clock_1 (.out(clk));
  Register #(.width(32)) register_1 (.D(multiplexer_1_out), .en(1'b1), .clk(clk), .Q(pc_q));  // open: clr
  Adder #(.width(32)) adder_1 (.a(32'h4), .b(pc_q), .out(pc_plus4));  // open: cin, cout
  Adder #(.width(32)) adder_2 (.a(pc_q), .b(u_im), .out(auipc_result), .cin(1'b0));  // open: cout
  Adder #(.width(32)) adder_3 (.a(pc_q), .b(sb_im), .out(branch_target), .cin(1'b0));  // open: cout
  Adder #(.width(32)) adder_4 (.a(pc_q), .b(j_im), .out(jal_target), .cin(1'b0));  // open: cout
  ROM #(.addrWidth(14), .dataWidth(32)) inst_mem (.addr(pc_q[15:2]), .data(inst_mem_data));
  Multiplexer #(.select(2), .width(32)) multiplexer_1 (
    .in0(pc_plus4), .in1(branch_target), .in2(jal_target), .in3(jalr_target), .out(multiplexer_1_out),
    .sel(pc_sel));
  detect_end detect_end_1 (.inst(inst_mem_data), .halt(out_1));
  inst_decoder inst_decoder_1 (
    .inst(inst_mem_data), .br_eq(br_eq), .blt(blt), .rs1(inst_decoder_1_rs1), .rs2(inst_decoder_1_rs2),
    .rd(inst_decoder_1_rd), .alu_fun(alu_fun), .wb_sel(wb_sel), .op2_sel(op2_sel), .ld_en(ld_en),
    .sw_en(sw_en), .pc_sel(pc_sel), .rf_we(rf_we), .s_im(s_im), .sb_im(sb_im), .i_im(i_im), .u_im(u_im),
    .j_im(j_im));  // open: bge
  // Probe on out_2
  // Probe on out_3
  // Probe on out_4
  // Probe on out_5
  rf32 rf32_1 (
    .ra1(inst_decoder_1_rs1), .ra2(inst_decoder_1_rs2), .wa(inst_decoder_1_rd), .we(rf_we),
    .wd(multiplexer_3_out), .clk(clk), .dx0(out_2), .dx1(out_3), .dx2(out_4), .dx3(out_5), .dx4(out_6),
    .dx5(out_7), .dx6(out_8), .dx7(out_9), .dx8(out_10), .dx9(out_11), .dx10(out_12), .rd1(rf32_1_rd1),
    .rd2(rf32_1_rd2));  // open: dx11, dx12, dx13, dx14, dx15, dx16, dx17, dx18, dx19, dx20, dx21, dx22, dx23, dx24, dx25, dx26, dx27, dx28, dx29, dx30, dx31
  // Probe on out_6
  // Probe on out_7
  // Probe on out_8
  // Probe on out_9
  Multiplexer #(.select(2), .width(32)) multiplexer_2 (
    .in0(rf32_1_rd2), .in1(i_im), .in2(s_im), .out(multiplexer_2_out), .sel(op2_sel));  // open: in3
  Comparator #(.width(32)) comparator_1 (.a(rf32_1_rd1), .b(rf32_1_rd2), .eq(br_eq), .lt(blt));  // open: gt
  // Probe on out_10
  assign jalr_target = jalr_sum & 32'hfffffffe;  // AND_Gate and_1, 32 bits wide
  alu alu_1 (.alu_in0(rf32_1_rd1), .alu_in1(multiplexer_2_out), .u_fun(alu_fun), .alu_out(alu_1_alu_out));
  Adder #(.width(32)) adder_5 (.a(rf32_1_rd1), .b(i_im), .out(jalr_sum), .cin(1'b0));  // open: cout
  RAM #(.addrWidth(14), .asyncread("true"), .dataWidth(32)) data_ram (
    .addr(alu_1_alu_out[15:2]), .we(sw_en), .oe(ld_en), .clk(clk), .din(rf32_1_rd2), .dout(data_ram_dout));
  Multiplexer #(.select(3), .width(32)) multiplexer_3 (
    .in0(alu_1_alu_out), .in1(data_ram_dout), .in2(auipc_result), .in3(pc_plus4), .out(multiplexer_3_out),
    .sel(wb_sel));  // open: in4, in5, in6, in7

  // Other names for the same wires on the sheet: x0[31:0] = out_2; x1[31:0] = out_3; x2[31:0] = out_4;
  //   x3[31:0] = out_5; x4[31:0] = out_6; x5[31:0] = out_7; x6[31:0] = out_8; x7[31:0] = out_9; x8[31:0] = out_10;
  //   x9[31:0] = out_11; x10[31:0] = out_12

  // Notes on the sheet:
  //   contents of inst_mem (hex, n*v repeats v):
  //   200e13 93 18000ef 13 100073 badbad0 13 13 c10113 100073 88888888
endmodule

module detect_end (
  input  [31:0] inst,
  output halt
);

  Comparator #(.mode("unsigned"), .width(32)) comparator_1 (.a(inst), .b(32'h100073), .eq(halt));  // open: gt, lt

  // Notes on the sheet:
  //   ebreak
endmodule

module inst_decoder (
  input  [31:0] inst,
  input  br_eq,
  input  blt,
  input  bge,
  output [4:0] rs1,
  output [4:0] rs2,
  output [4:0] rd,
  output [2:0] alu_fun,
  output [2:0] wb_sel,
  output [1:0] op2_sel,
  output ld_en,
  output sw_en,
  output [1:0] pc_sel,
  output rf_we,
  output [31:0] s_im,
  output [31:0] sb_im,
  output [31:0] i_im,
  output [31:0] u_im,
  output [31:0] j_im
);

  wire add, addi, \and , and_1_out, auipc, beq, beq_taken, bge_taken, blt_taken, bne, bne_taken,
       branch_taken, comparator_1_eq, comparator_2_eq, comparator_3_eq, comparator_4_eq, comparator_5_eq,
       comparator_6_eq, comparator_7_eq, comparator_8_eq, comparator_9_eq, comparator_10_eq,
       comparator_11_eq, comparator_12_eq, comparator_13_eq, comparator_14_eq, comparator_16_eq,
       comparator_17_eq, comparator_19_eq, comparator_20_eq, comparator_21_eq, comparator_22_eq,
       comparator_23_eq, comparator_24_eq, comparator_26_eq, comparator_27_eq, comparator_28_eq,
       comparator_29_eq, comparator_30_eq, comparator_31_eq, is_bge, is_blt, isRtype, jal, jalr, link,
       not_1_out, not_2_out, \or , or_2_out, sub;

  Priority_Encoder priority_encoder_1 (
    .in0(sub), .in1(add), .in2(\or ), .in3(\and ), .in4(1'b0), .in5(1'b0), .in6(1'b0), .in7(1'b0),
    .out(alu_fun), .en_in(1'b1));  // open: gs, en_out
  Comparator #(.width(7)) comparator_1 (.a(inst[6:0]), .b(7'b0110011), .eq(comparator_1_eq));  // open: gt, lt
  Comparator #(.width(3)) comparator_2 (.a(inst[14:12]), .b(3'b000), .eq(comparator_2_eq));  // open: gt, lt
  Comparator #(.width(7)) comparator_3 (.a(inst[31:25]), .b({7{1'b0}}), .eq(comparator_3_eq));  // open: gt, lt
  Comparator #(.width(7)) comparator_4 (.a(inst[6:0]), .b(7'b0110011), .eq(comparator_4_eq));  // open: gt, lt
  Comparator #(.width(3)) comparator_5 (.a(inst[14:12]), .b(3'b000), .eq(comparator_5_eq));  // open: gt, lt
  Comparator #(.width(7)) comparator_6 (.a(inst[31:25]), .b(7'b0100000), .eq(comparator_6_eq));  // open: gt, lt
  Comparator #(.width(7)) comparator_7 (.a(inst[6:0]), .b(7'b0110011), .eq(comparator_7_eq));  // open: gt, lt
  Comparator #(.width(3)) comparator_8 (.a(inst[14:12]), .b(3'b111), .eq(comparator_8_eq));  // open: gt, lt
  Comparator #(.width(7)) comparator_9 (.a(inst[31:25]), .b({7{1'b0}}), .eq(comparator_9_eq));  // open: gt, lt
  Comparator #(.width(7)) comparator_10 (.a(inst[6:0]), .b(7'b0110011), .eq(comparator_10_eq));  // open: gt, lt
  Comparator #(.width(3)) comparator_11 (.a(inst[14:12]), .b(3'b110), .eq(comparator_11_eq));  // open: gt, lt
  Comparator #(.width(7)) comparator_12 (.a(inst[31:25]), .b({7{1'b0}}), .eq(comparator_12_eq));  // open: gt, lt
  Comparator #(.width(7)) comparator_13 (.a(inst[6:0]), .b(7'b0000011), .eq(comparator_13_eq));  // open: gt, lt
  Comparator #(.width(3)) comparator_14 (.a(inst[14:12]), .b(3'b010), .eq(comparator_14_eq));  // open: gt, lt
  and and_1 (and_1_out, comparator_1_eq, comparator_2_eq, comparator_3_eq);
  and and_2 (sub, comparator_4_eq, comparator_5_eq, comparator_6_eq);
  and and_3 (\and , comparator_7_eq, comparator_8_eq, comparator_9_eq);
  and and_4 (\or , comparator_10_eq, comparator_11_eq, comparator_12_eq);
  Comparator #(.width(7)) comparator_15 (.a(inst[6:0]), .b(7'b0010111), .eq(auipc));  // open: gt, lt
  assign u_im = inst & 32'hfffff000;  // AND_Gate and_5, 32 bits wide
  and and_6 (ld_en, comparator_13_eq, comparator_14_eq);
  or or_1 (add, and_1_out, ld_en, sw_en, addi);
  or or_2 (or_2_out, addi, ld_en);
  Comparator #(.width(7)) comparator_16 (.a(inst[6:0]), .b(7'b0010011), .eq(comparator_16_eq));  // open: gt, lt
  Comparator #(.width(3)) comparator_17 (.a(inst[14:12]), .b(3'b000), .eq(comparator_17_eq));  // open: gt, lt
  Comparator #(.width(7)) comparator_18 (.a(inst[6:0]), .b(7'b0110011), .eq(isRtype));  // open: gt, lt
  Priority_Encoder #(.select(2)) priority_encoder_2 (
    .in0(isRtype), .in1(or_2_out), .in2(sw_en), .in3(1'b0), .out(op2_sel), .en_in(1'b1));  // open: gs, en_out
  or or_3 (rf_we, isRtype, addi, link, ld_en, auipc);
  Priority_Encoder priority_encoder_3 (
    .in0(1'b1), .in1(ld_en), .in2(auipc), .in3(link), .in4(1'b0), .in5(1'b0), .in6(1'b0), .in7(1'b0),
    .out(wb_sel), .en_in(1'b1));  // open: gs, en_out
  and and_7 (addi, comparator_16_eq, comparator_17_eq);
  Comparator #(.width(7)) comparator_19 (.a(inst[6:0]), .b(7'b1100111), .eq(comparator_19_eq));  // open: gt, lt
  Comparator #(.width(3)) comparator_20 (.a(inst[14:12]), .b(3'b000), .eq(comparator_20_eq));  // open: gt, lt
  Comparator #(.width(7)) comparator_21 (.a(inst[6:0]), .b(7'b0100011), .eq(comparator_21_eq));  // open: gt, lt
  Comparator #(.width(3)) comparator_22 (.a(inst[14:12]), .b(3'b010), .eq(comparator_22_eq));  // open: gt, lt
  Comparator #(.width(7)) comparator_23 (.a(inst[6:0]), .b(7'b1100011), .eq(comparator_23_eq));  // open: gt, lt
  Comparator #(.width(3)) comparator_24 (.a(inst[14:12]), .b(3'b000), .eq(comparator_24_eq));  // open: gt, lt
  and and_8 (jalr, comparator_19_eq, comparator_20_eq);
  and and_9 (sw_en, comparator_21_eq, comparator_22_eq);
  and and_10 (beq, comparator_23_eq, comparator_24_eq);
  and and_11 (beq_taken, beq, br_eq);
  Priority_Encoder #(.select(2)) priority_encoder_4 (
    .in0(1'b1), .in1(branch_taken), .in2(jal), .in3(jalr), .out(pc_sel), .en_in(1'b1));  // open: gs, en_out
  Comparator #(.width(7)) comparator_25 (.a(inst[6:0]), .b(7'b1101111), .eq(jal));  // open: gt, lt
  or or_4 (link, jal, jalr);
  Comparator #(.width(7)) comparator_26 (.a(inst[6:0]), .b(7'b1100011), .eq(comparator_26_eq));  // open: gt, lt
  Comparator #(.width(3)) comparator_27 (.a(inst[14:12]), .b(3'b101), .eq(comparator_27_eq));  // open: gt, lt
  Comparator #(.width(7)) comparator_28 (.a(inst[6:0]), .b(7'b1100011), .eq(comparator_28_eq));  // open: gt, lt
  Comparator #(.width(3)) comparator_29 (.a(inst[14:12]), .b(3'b100), .eq(comparator_29_eq));  // open: gt, lt
  Comparator #(.width(7)) comparator_30 (.a(inst[6:0]), .b(7'b1100011), .eq(comparator_30_eq));  // open: gt, lt
  Comparator #(.width(3)) comparator_31 (.a(inst[14:12]), .b(3'b001), .eq(comparator_31_eq));  // open: gt, lt
  not not_1 (not_1_out, br_eq);
  and and_12 (is_bge, comparator_26_eq, comparator_27_eq);
  and and_13 (is_blt, comparator_28_eq, comparator_29_eq);
  and and_14 (bne, comparator_30_eq, comparator_31_eq);
  and and_15 (bne_taken, not_1_out, bne);
  or or_5 (branch_taken, beq_taken, blt_taken, bge_taken, bne_taken);
  not not_2 (not_2_out, blt);
  and and_16 (blt_taken, is_blt, blt);
  and and_17 (bge_taken, not_2_out, is_bge);

  assign i_im = {{21{inst[31]}}, inst[30:20]};
  assign j_im = {{12{inst[31]}}, inst[19:12], inst[20], inst[30:21], 1'b0};
  assign rd = inst[11:7];
  assign rs1 = inst[19:15];
  assign rs2 = inst[24:20];
  assign s_im = {{21{inst[31]}}, inst[30:25], inst[11:7]};
  assign sb_im = {{20{inst[31]}}, inst[7], inst[30:25], inst[11:8], 1'b0};

  // Other names for the same wires on the sheet: inst_word[31:0] = inst; fun7[6:0] = inst[31:25];
  //   fun3[2:0] = inst[14:12]; lw = ld_en; op[6:0] = inst[6:0]; sw = sw_en

  // Notes on the sheet:
  //   When the instruction is ADD
  //   When the instruction is SUB
  //   When the instruction is AND
  //   When the instruction is OR
  //   When the instruction is ADDi
endmodule
