// Logisim project rv32_isu.circ as structural Verilog: 3 circuits, main circuit main
module main (
  output out_1,
  output [31:0] out_2,
  output [31:0] out_3,
  output [31:0] out_4,
  output [31:0] out_5,
  output [31:0] out_6,
  output [31:0] out_7,
  output [31:0] out_8,
  output [31:0] out_9,
  output [31:0] out_10,
  output [31:0] out_11,
  output [31:0] out_12
);

  wire clk, ld_en, rf_we, sw_en;
  wire [1:0] op2_sel;
  wire [2:0] alu_fun, wb_sel;
  wire [4:0] inst_decoder_1_rd, inst_decoder_1_rs1, inst_decoder_1_rs2;
  wire [31:0] adder_1_out, alu_1_alu_out, auipc_result, data_ram_dout, i_im, inst_mem_data,
       multiplexer_1_out, multiplexer_2_out, register_1_q, rf32_1_rd1, rf32_1_rd2, s_im, u_im;

  Clock clock_1 (.out(clk));
  Register #(.width(32)) register_1 (.D(adder_1_out), .en(1'b1), .clk(clk), .Q(register_1_q));  // open: clr
  Adder #(.width(32)) adder_1 (.a(32'h4), .b(register_1_q), .out(adder_1_out));  // open: cin, cout
  Adder #(.width(32)) adder_2 (.a(register_1_q), .b(u_im), .out(auipc_result), .cin(1'b0));  // open: cout
  ROM #(.addrWidth(14), .dataWidth(32)) inst_mem (.addr(register_1_q[15:2]), .data(inst_mem_data));
  detect_end detect_end_1 (.inst(inst_mem_data), .halt(out_1));
  inst_decoder inst_decoder_1 (
    .inst(inst_mem_data), .rs1(inst_decoder_1_rs1), .rs2(inst_decoder_1_rs2), .rd(inst_decoder_1_rd),
    .alu_fun(alu_fun), .wb_sel(wb_sel), .op2_sel(op2_sel), .ld_en(ld_en), .sw_en(sw_en), .rf_we(rf_we),
    .s_im(s_im), .i_im(i_im), .u_im(u_im));  // open: br_eq, blt, bge, pc_sel, sb_im, j_im
  // Probe on out_2
  // Probe on out_3
  // Probe on out_4
  // Probe on out_5
  rf32 rf32_1 (
    .ra1(inst_decoder_1_rs1), .ra2(inst_decoder_1_rs2), .wa(inst_decoder_1_rd), .we(rf_we),
    .wd(multiplexer_2_out), .clk(clk), .dx0(out_2), .dx1(out_3), .dx2(out_4), .dx3(out_5), .dx4(out_6),
    .dx5(out_7), .dx6(out_8), .dx7(out_9), .dx8(out_10), .dx9(out_11), .dx10(out_12), .rd1(rf32_1_rd1),
    .rd2(rf32_1_rd2));  // open: dx11, dx12, dx13, dx14, dx15, dx16, dx17, dx18, dx19, dx20, dx21, dx22, dx23, dx24, dx25, dx26, dx27, dx28, dx29, dx30, dx31
  // Probe on out_6
  // Probe on out_7
  // Probe on out_8
  // Probe on out_9
  Multiplexer #(.select(2), .width(32)) multiplexer_1 (
    .in0(rf32_1_rd2), .in1(i_im), .in2(s_im), .out(multiplexer_1_out), .sel(op2_sel));  // open: in3
  // Probe on out_10
  alu alu_1 (.alu_in0(rf32_1_rd1), .alu_in1(multiplexer_1_out), .u_fun(alu_fun), .alu_out(alu_1_alu_out));
  RAM #(.addrWidth(14), .asyncread("true"), .dataWidth(32)) data_ram (
    .addr(alu_1_alu_out[15:2]), .we(sw_en), .oe(ld_en), .clk(clk), .din(rf32_1_rd2), .dout(data_ram_dout));
  Multiplexer #(.select(3), .width(32)) multiplexer_2 (
    .in0(alu_1_alu_out), .in1(data_ram_dout), .in2(auipc_result), .out(multiplexer_2_out), .sel(wb_sel));  // open: in3, in4, in5, in6, in7

  // Other names for the same wires on the sheet: x0[31:0] = out_2; x1[31:0] = out_3; x2[31:0] = out_4;
  //   x3[31:0] = out_5; x4[31:0] = out_6; x5[31:0] = out_7; x6[31:0] = out_8; x7[31:0] = out_9; x8[31:0] = out_10;
  //   x9[31:0] = out_11; x10[31:0] = out_12

  // Notes on the sheet:
  //   contents of inst_mem (hex, n*v repeats v):
  //   1000093 4200113 20a023 110113 20a223 110113 20a423 100073
endmodule

module detect_end (
  input  [31:0] inst,
  output halt
);

  Comparator #(.mode("unsigned"), .width(32)) comparator_1 (.a(inst), .b(32'h100073), .eq(halt));  // open: gt, lt

  // Notes on the sheet:
  //   ebreak
endmodule

module inst_decoder (
  input  [31:0] inst,
  input  br_eq,
  input  blt,
  input  bge,
  output [4:0] rs1,
  output [4:0] rs2,
  output [4:0] rd,
  output [2:0] alu_fun,
  output [2:0] wb_sel,
  output [1:0] op2_sel,
  output ld_en,
  output sw_en,
  output [1:0] pc_sel,
  output rf_we,
  output [31:0] s_im,
  output [31:0] sb_im,
  output [31:0] i_im,
  output [31:0] u_im,
  output [31:0] j_im
);

  wire add, addi, \and , and_1_out, auipc, comparator_1_eq, comparator_2_eq, comparator_3_eq,
       comparator_4_eq, comparator_5_eq, comparator_6_eq, comparator_7_eq, comparator_8_eq, comparator_9_eq,
       comparator_10_eq, comparator_11_eq, comparator_12_eq, comparator_13_eq, comparator_14_eq,
       comparator_16_eq, comparator_17_eq, comparator_19_eq, comparator_20_eq, isRtype, \or , or_2_out, sub;

  Priority_Encoder priority_encoder_1 (
    .in0(sub), .in1(add), .in2(\or ), .in3(\and ), .in4(1'b0), .in5(1'b0), .in6(1'b0), .in7(1'b0),
    .out(alu_fun), .en_in(1'b1));  // open: gs, en_out
  Comparator #(.width(7)) comparator_1 (.a(inst[6:0]), .b(7'b0110011), .eq(comparator_1_eq));  // open: gt, lt
  Comparator #(.width(3)) comparator_2 (.a(inst[14:12]), .b(3'b000), .eq(comparator_2_eq));  // open: gt, lt
  Comparator #(.width(7)) comparator_3 (.a(inst[31:25]), .b({7{1'b0}}), .eq(comparator_3_eq));  // open: gt, lt
  Comparator #(.width(7)) comparator_4 (.a(inst[6:0]), .b(7'b0110011), .eq(comparator_4_eq));  // open: gt, lt
  Comparator #(.width(3)) comparator_5 (.a(inst[14:12]), .b(3'b000), .eq(comparator_5_eq));  // open: gt, lt
  Comparator #(.width(7)) comparator_6 (.a(inst[31:25]), .b(7'b0100000), .eq(comparator_6_eq));  // open: gt, lt
  Comparator #(.width(7)) comparator_7 (.a(inst[6:0]), .b(7'b0110011), .eq(comparator_7_eq));  // open: gt, lt
  Comparator #(.width(3)) comparator_8 (.a(inst[14:12]), .b(3'b111), .eq(comparator_8_eq));  // open: gt, lt
  Comparator #(.width(7)) comparator_9 (.a(inst[31:25]), .b({7{1'b0}}), .eq(comparator_9_eq));  // open: gt, lt
  Comparator #(.width(7)) comparator_10 (.a(inst[6:0]), .b(7'b0110011), .eq(comparator_10_eq));  // open: gt, lt
  Comparator #(.width(3)) comparator_11 (.a(inst[14:12]), .b(3'b110), .eq(comparator_11_eq));  // open: gt, lt
  Comparator #(.width(7)) comparator_12 (.a(inst[31:25]), .b({7{1'b0}}), .eq(comparator_12_eq));  // open: gt, lt
  Comparator #(.width(7)) comparator_13 (.a(inst[6:0]), .b(7'b0000011), .eq(comparator_13_eq));  // open: gt, lt
  Comparator #(.width(3)) comparator_14 (.a(inst[14:12]), .b(3'b010), .eq(comparator_14_eq));  // open: gt, lt
  and and_1 (and_1_out, comparator_1_eq, comparator_2_eq, comparator_3_eq);
  and and_2 (sub, comparator_4_eq, comparator_5_eq, comparator_6_eq);
  and and_3 (\and , comparator_7_eq, comparator_8_eq, comparator_9_eq);
  and and_4 (\or , comparator_10_eq, comparator_11_eq, comparator_12_eq);
  Comparator #(.width(7)) comparator_15 (.a(inst[6:0]), .b(7'b0010111), .eq(auipc));  // open: gt, lt
  assign u_im = inst & 32'hfffff000;  // AND_Gate and_5, 32 bits wide
  and and_6 (ld_en, comparator_13_eq, comparator_14_eq);
  or or_1 (add, and_1_out, ld_en, sw_en, addi);
  or or_2 (or_2_out, addi, ld_en);
  Comparator #(.width(7)) comparator_16 (.a(inst[6:0]), .b(7'b0010011), .eq(comparator_16_eq));  // open: gt, lt
  Comparator #(.width(3)) comparator_17 (.a(inst[14:12]), .b(3'b000), .eq(comparator_17_eq));  // open: gt, lt
  Comparator #(.width(7)) comparator_18 (.a(inst[6:0]), .b(7'b0110011), .eq(isRtype));  // open: gt, lt
  Priority_Encoder #(.select(2)) priority_encoder_2 (
    .in0(isRtype), .in1(or_2_out), .in2(sw_en), .in3(1'b0), .out(op2_sel), .en_in(1'b1));  // open: gs, en_out
  or or_3 (rf_we, isRtype, addi, ld_en, auipc);
  Priority_Encoder priority_encoder_3 (
    .in0(1'b1), .in1(ld_en), .in2(auipc), .in3(1'b0), .in4(1'b0), .in5(1'b0), .in6(1'b0), .in7(1'b0),
    .out(wb_sel), .en_in(1'b1));  // open: gs, en_out
  and and_7 (addi, comparator_16_eq, comparator_17_eq);
  Comparator #(.width(7)) comparator_19 (.a(inst[6:0]), .b(7'b0100011), .eq(comparator_19_eq));  // open: gt, lt
  Comparator #(.width(3)) comparator_20 (.a(inst[14:12]), .b(3'b010), .eq(comparator_20_eq));  // open: gt, lt
  and and_8 (sw_en, comparator_19_eq, comparator_20_eq);

  assign i_im = {{21{inst[31]}}, inst[30:20]};
  assign rd = inst[11:7];
  assign rs1 = inst[19:15];
  assign rs2 = inst[24:20];
  assign s_im = {{21{inst[31]}}, inst[30:25], inst[11:7]};

  // Other names for the same wires on the sheet: fun3[2:0] = inst[14:12]; inst_word[31:0] = inst; lw = ld_en;
  //   op[6:0] = inst[6:0]; fun7[6:0] = inst[31:25]; sw = sw_en

  // Notes on the sheet:
  //   When the instruction is ADD
  //   When the instruction is SUB
  //   When the instruction is AND
  //   When the instruction is OR
  //   When the instruction is ADDi
endmodule
