// Logisim project uproclib.circ as structural Verilog: 8 circuits, main circuit and8
module and8 (
  input  [7:0] in0,
  input  [7:0] in1,
  output [7:0] out0
);

  and and_1 (out0[0], in0[0], in1[0]);
  and and_2 (out0[1], in0[1], in1[1]);
  and and_3 (out0[2], in0[2], in1[2]);
  and and_4 (out0[3], in0[3], in1[3]);
  and and_5 (out0[4], in0[4], in1[4]);
  and and_6 (out0[5], in0[5], in1[5]);
  and and_7 (out0[6], in0[6], in1[6]);
  and and_8 (out0[7], in0[7], in1[7]);
endmodule

module and32 (
  input  [31:0] in0,
  input  [31:0] in1,
  output [31:0] out0
);

  and8 and8_1 (.in0(in0[7:0]), .in1(in1[7:0]), .out0(out0[7:0]));
  and8 and8_2 (.in0(in0[15:8]), .in1(in1[15:8]), .out0(out0[15:8]));
  and8 and8_3 (.in0(in0[23:16]), .in1(in1[23:16]), .out0(out0[23:16]));
  and8 and8_4 (.in0(in0[31:24]), .in1(in1[31:24]), .out0(out0[31:24]));
endmodule

module or8 (
  input  [7:0] in0,
  input  [7:0] in1,
  output [7:0] out0
);

  or or_1 (out0[0], in0[0], in1[0]);
  or or_2 (out0[1], in0[1], in1[1]);
  or or_3 (out0[2], in0[2], in1[2]);
  or or_4 (out0[3], in0[3], in1[3]);
  or or_5 (out0[4], in0[4], in1[4]);
  or or_6 (out0[5], in0[5], in1[5]);
  or or_7 (out0[6], in0[6], in1[6]);
  or or_8 (out0[7], in0[7], in1[7]);
endmodule

module or32 (
  input  [31:0] in0,
  input  [31:0] in1,
  output [31:0] out0
);

  or8 or8_1 (.in0(in0[7:0]), .in1(in1[7:0]), .out0(out0[7:0]));
  or8 or8_2 (.in0(in0[15:8]), .in1(in1[15:8]), .out0(out0[15:8]));
  or8 or8_3 (.in0(in0[23:16]), .in1(in1[23:16]), .out0(out0[23:16]));
  or8 or8_4 (.in0(in0[31:24]), .in1(in1[31:24]), .out0(out0[31:24]));
endmodule

module alu (
  input  [31:0] alu_in0,
  input  [31:0] alu_in1,
  input  [2:0] u_fun,
  output [31:0] alu_out
);

  wire [31:0] adder_1_out, and32_1_out0, or32_1_out0, shifter_1_out, subtractor_1_out;

  Subtractor #(.width(32)) subtractor_1 (.a(alu_in0), .b(alu_in1), .out(subtractor_1_out), .bin(1'b0));  // open: bout
  Adder #(.width(32)) adder_1 (.a(alu_in0), .b(alu_in1), .out(adder_1_out));  // open: cin, cout
  or32 or32_1 (.in0(alu_in0), .in1(alu_in1), .out0(or32_1_out0));
  and32 and32_1 (.in0(alu_in0), .in1(alu_in1), .out0(and32_1_out0));
  Shifter #(.width(32)) shifter_1 (.in(alu_in0), .\dist (alu_in1[4:0]), .out(shifter_1_out));
  Multiplexer #(.enable("true"), .select(3), .width(32)) multiplexer_1 (
    .in0(subtractor_1_out), .in1(adder_1_out), .in2(or32_1_out0), .in3(and32_1_out0), .in4(shifter_1_out),
    .in5({32{1'b0}}), .in6({32{1'b0}}), .in7({32{1'b0}}), .out(alu_out), .sel(u_fun), .en(1'b1));
endmodule

module rf8 (
  input  [2:0] ra1,
  input  [2:0] ra2,
  input  [31:0] wd,
  input  [2:0] wa,
  input  clk,
  input  we,
  output [31:0] rd1,
  output [31:0] rd2,
  output [31:0] dx0,
  output [31:0] dx1,
  output [31:0] dx2,
  output [31:0] dx3,
  output [31:0] dx4,
  output [31:0] dx5,
  output [31:0] dx6,
  output [31:0] dx7
);

  wire [7:0] and8_1_out0, decoder_1_out0;
  wire [31:0] demultiplexer_1_out0, demultiplexer_1_out1, demultiplexer_1_out2, demultiplexer_1_out3,
       demultiplexer_1_out4, demultiplexer_1_out5, demultiplexer_1_out6, demultiplexer_1_out7,
       multiplexer_1_out;

  Demultiplexer #(.enable("true"), .select(3), .width(32)) demultiplexer_1 (
    .out0(demultiplexer_1_out0), .out1(demultiplexer_1_out1), .out2(demultiplexer_1_out2),
    .out3(demultiplexer_1_out3), .out4(demultiplexer_1_out4), .out5(demultiplexer_1_out5),
    .out6(demultiplexer_1_out6), .out7(demultiplexer_1_out7), .in(wd), .sel(wa), .en(1'b1));
  Decoder #(.select(3)) decoder_1 (
    .out0(decoder_1_out0[0]), .out1(decoder_1_out0[1]), .out2(decoder_1_out0[2]), .out3(decoder_1_out0[3]),
    .out4(decoder_1_out0[4]), .out5(decoder_1_out0[5]), .out6(decoder_1_out0[6]), .out7(decoder_1_out0[7]),
    .sel(wa), .en(1'b1));
  Multiplexer #(.enable("true"), .width(32)) multiplexer_1 (
    .in0({32{1'b0}}), .in1(demultiplexer_1_out0), .out(multiplexer_1_out), .sel(1'b1), .en(1'b1));
  and8 and8_1 (.in0(decoder_1_out0), .in1({8{we}}), .out0(and8_1_out0));
  Register #(.width(32)) register_1 (.D(multiplexer_1_out), .en(and8_1_out0[0]), .clk(clk), .Q(dx0), .clr(1'b0));
  Register #(.width(32)) register_2 (.D(demultiplexer_1_out2), .en(and8_1_out0[2]), .clk(clk), .Q(dx2));  // open: clr
  Register #(.width(32)) register_3 (.D(demultiplexer_1_out4), .en(and8_1_out0[4]), .clk(clk), .Q(dx4), .clr(1'b0));
  Register #(.width(32)) register_4 (.D(demultiplexer_1_out6), .en(and8_1_out0[6]), .clk(clk), .Q(dx6), .clr(1'b0));
  Register #(.width(32)) register_5 (.D(demultiplexer_1_out1), .en(and8_1_out0[1]), .clk(clk), .Q(dx1), .clr(1'b0));
  Register #(.width(32)) register_6 (.D(demultiplexer_1_out3), .en(and8_1_out0[3]), .clk(clk), .Q(dx3), .clr(1'b0));
  Register #(.width(32)) register_7 (.D(demultiplexer_1_out5), .en(and8_1_out0[5]), .clk(clk), .Q(dx5), .clr(1'b0));
  Register #(.width(32)) register_8 (.D(demultiplexer_1_out7), .en(and8_1_out0[7]), .clk(clk), .Q(dx7), .clr(1'b0));
  Multiplexer #(.enable("true"), .select(3), .width(32)) multiplexer_2 (
    .in0(dx0), .in1(dx1), .in2(dx2), .in3(dx3), .in4(dx4), .in5(dx5), .in6(dx6), .in7(dx7), .out(rd1),
    .sel(ra1), .en(1'b1));
  Multiplexer #(.enable("true"), .select(3), .width(32)) multiplexer_3 (
    .in0(dx0), .in1(dx1), .in2(dx2), .in3(dx3), .in4(dx4), .in5(dx5), .in6(dx6), .in7(dx7), .out(rd2),
    .sel(ra2), .en(1'b1));
endmodule

module rf8_0 (
  input  [2:0] ra1,
  input  [2:0] ra2,
  input  [31:0] wd,
  input  [2:0] wa,
  input  clk,
  input  we,
  output [31:0] rd1,
  output [31:0] rd2,
  output [31:0] dx0,
  output [31:0] dx1,
  output [31:0] dx2,
  output [31:0] dx3,
  output [31:0] dx4,
  output [31:0] dx5,
  output [31:0] dx6,
  output [31:0] dx7
);

  wire [7:0] and8_1_out0, decoder_1_out0;
  wire [31:0] demultiplexer_1_out0, demultiplexer_1_out1, demultiplexer_1_out2, demultiplexer_1_out3,
       demultiplexer_1_out4, demultiplexer_1_out5, demultiplexer_1_out6, demultiplexer_1_out7,
       multiplexer_1_out;

  Demultiplexer #(.enable("true"), .select(3), .width(32)) demultiplexer_1 (
    .out0(demultiplexer_1_out0), .out1(demultiplexer_1_out1), .out2(demultiplexer_1_out2),
    .out3(demultiplexer_1_out3), .out4(demultiplexer_1_out4), .out5(demultiplexer_1_out5),
    .out6(demultiplexer_1_out6), .out7(demultiplexer_1_out7), .in(wd), .sel(wa), .en(1'b1));
  Decoder #(.select(3)) decoder_1 (
    .out0(decoder_1_out0[0]), .out1(decoder_1_out0[1]), .out2(decoder_1_out0[2]), .out3(decoder_1_out0[3]),
    .out4(decoder_1_out0[4]), .out5(decoder_1_out0[5]), .out6(decoder_1_out0[6]), .out7(decoder_1_out0[7]),
    .sel(wa), .en(1'b1));
  Multiplexer #(.enable("true"), .width(32)) multiplexer_1 (
    .in0({32{1'b0}}), .in1(demultiplexer_1_out0), .out(multiplexer_1_out), .sel(1'b0), .en(1'b1));
  and8 and8_1 (.in0(decoder_1_out0), .in1({8{we}}), .out0(and8_1_out0));
  Register #(.width(32)) register_1 (.D(multiplexer_1_out), .en(and8_1_out0[0]), .clk(clk), .Q(dx0), .clr(1'b0));
  Register #(.width(32)) register_2 (.D(demultiplexer_1_out2), .en(and8_1_out0[2]), .clk(clk), .Q(dx2));  // open: clr
  Register #(.width(32)) register_3 (.D(demultiplexer_1_out4), .en(and8_1_out0[4]), .clk(clk), .Q(dx4), .clr(1'b0));
  Register #(.width(32)) register_4 (.D(demultiplexer_1_out6), .en(and8_1_out0[6]), .clk(clk), .Q(dx6), .clr(1'b0));
  Register #(.width(32)) register_5 (.D(demultiplexer_1_out1), .en(and8_1_out0[1]), .clk(clk), .Q(dx1), .clr(1'b0));
  Register #(.width(32)) register_6 (.D(demultiplexer_1_out3), .en(and8_1_out0[3]), .clk(clk), .Q(dx3), .clr(1'b0));
  Register #(.width(32)) register_7 (.D(demultiplexer_1_out5), .en(and8_1_out0[5]), .clk(clk), .Q(dx5), .clr(1'b0));
  Register #(.width(32)) register_8 (.D(demultiplexer_1_out7), .en(and8_1_out0[7]), .clk(clk), .Q(dx7), .clr(1'b0));
  Multiplexer #(.enable("true"), .select(3), .width(32)) multiplexer_2 (
    .in0(dx0), .in1(dx1), .in2(dx2), .in3(dx3), .in4(dx4), .in5(dx5), .in6(dx6), .in7(dx7), .out(rd1),
    .sel(ra1), .en(1'b1));
  Multiplexer #(.enable("true"), .select(3), .width(32)) multiplexer_3 (
    .in0(dx0), .in1(dx1), .in2(dx2), .in3(dx3), .in4(dx4), .in5(dx5), .in6(dx6), .in7(dx7), .out(rd2),
    .sel(ra2), .en(1'b1));
endmodule

module rf32 (
  input  [4:0] ra1,
  input  [4:0] ra2,
  input  [4:0] wa,
  input  we,
  input  [31:0] wd,
  input  clk,
  output [31:0] dx0,
  output [31:0] dx1,
  output [31:0] dx2,
  output [31:0] dx3,
  output [31:0] dx4,
  output [31:0] dx5,
  output [31:0] dx6,
  output [31:0] dx7,
  output [31:0] dx8,
  output [31:0] dx9,
  output [31:0] dx10,
  output [31:0] dx11,
  output [31:0] dx12,
  output [31:0] dx13,
  output [31:0] dx14,
  output [31:0] dx15,
  output [31:0] rd1,
  output [31:0] rd2,
  output [31:0] dx16,
  output [31:0] dx17,
  output [31:0] dx18,
  output [31:0] dx19,
  output [31:0] dx20,
  output [31:0] dx21,
  output [31:0] dx22,
  output [31:0] dx23,
  output [31:0] dx24,
  output [31:0] dx25,
  output [31:0] dx26,
  output [31:0] dx27,
  output [31:0] dx28,
  output [31:0] dx29,
  output [31:0] dx30,
  output [31:0] dx31
);

  wire decoder_1_out0, decoder_1_out1, decoder_1_out2, decoder_1_out3, we0, we1, we2, we3;
  wire [2:0] ra1_0, ra1_1, ra1_2, ra1_3, ra2_0, ra2_1, ra2_2, ra2_3, wa2_0, wa2_1, wa2_2, wa2_3;
  wire [31:0] rd1_0, rd1_1, rd1_2, rd1_3, rd2_0, rd2_1, rd2_2, rd2_3;

  Decoder #(.select(2)) decoder_1 (
    .out0(decoder_1_out0), .out1(decoder_1_out1), .out2(decoder_1_out2), .out3(decoder_1_out3),
    .sel(wa[4:3]), .en(1'b1));
  Demultiplexer #(.enable("true"), .select(2), .width(3)) demultiplexer_1 (
    .out0(ra1_0), .out1(ra1_1), .out2(ra1_2), .out3(ra1_3), .in(ra1[2:0]), .sel(ra1[4:3]), .en(1'b1));
  Demultiplexer #(.enable("true"), .select(2), .width(3)) demultiplexer_2 (
    .out0(ra2_0), .out1(ra2_1), .out2(ra2_2), .out3(ra2_3), .in(ra2[2:0]), .sel(ra2[4:3]), .en(1'b1));
  Demultiplexer #(.enable("true"), .select(2), .width(3)) demultiplexer_3 (
    .out0(wa2_0), .out1(wa2_1), .out2(wa2_2), .out3(wa2_3), .in(wa[2:0]), .sel(wa[4:3]), .en(1'b1));
  and and_1 (we0, decoder_1_out0, we);
  and and_2 (we1, decoder_1_out1, we);
  and and_3 (we2, decoder_1_out2, we);
  and and_4 (we3, decoder_1_out3, we);
  rf8_0 rf8_0_1 (
    .ra1(ra1_0), .ra2(ra2_0), .wd(wd), .wa(wa2_0), .clk(clk), .we(we0), .rd1(rd1_0), .rd2(rd2_0), .dx0(dx0),
    .dx1(dx1), .dx2(dx2), .dx3(dx3), .dx4(dx4), .dx5(dx5), .dx6(dx6), .dx7(dx7));
  rf8 rf8_1 (
    .ra1(ra1_1), .ra2(ra2_1), .wd(wd), .wa(wa2_1), .clk(clk), .we(we1), .rd1(rd1_1), .rd2(rd2_1), .dx0(dx8),
    .dx1(dx9), .dx2(dx10), .dx3(dx11), .dx4(dx12), .dx5(dx13), .dx6(dx14), .dx7(dx15));
  rf8 rf8_2 (
    .ra1(ra1_2), .ra2(ra2_2), .wd(wd), .wa(wa2_2), .clk(clk), .we(we2), .rd1(rd1_2), .rd2(rd2_2), .dx0(dx16),
    .dx1(dx17), .dx2(dx18), .dx3(dx19), .dx4(dx20), .dx5(dx21), .dx6(dx22), .dx7(dx23));
  rf8 rf8_3 (
    .ra1(ra1_3), .ra2(ra2_3), .wd(wd), .wa(wa2_3), .clk(clk), .we(we3), .rd1(rd1_3), .rd2(rd2_3), .dx0(dx24),
    .dx1(dx25), .dx2(dx26), .dx3(dx27), .dx4(dx28), .dx5(dx29), .dx6(dx30), .dx7(dx31));
  Multiplexer #(.enable("true"), .select(2), .width(32)) multiplexer_1 (
    .in0(rd1_0), .in1(rd1_1), .in2(rd1_2), .in3(rd1_3), .out(rd1), .sel(ra1[4:3]), .en(1'b1));
  Multiplexer #(.enable("true"), .select(2), .width(32)) multiplexer_2 (
    .in0(rd2_0), .in1(rd2_1), .in2(rd2_2), .in3(rd2_3), .out(rd2), .sel(ra2[4:3]), .en(1'b1));

  // Other names for the same wires on the sheet: x0[31:0] = dx0; x1[31:0] = dx1; x2[31:0] = dx2; x3[31:0] = dx3;
  //   x4[31:0] = dx4; x5[31:0] = dx5; x6[31:0] = dx6; x7[31:0] = dx7; x8[31:0] = dx8; x9[31:0] = dx9;
  //   x10[31:0] = dx10; x11[31:0] = dx11; x12[31:0] = dx12; x13[31:0] = dx13; x14[31:0] = dx14; x15[31:0] = dx15;
  //   x16[31:0] = dx16; x17[31:0] = dx17; x18[31:0] = dx18; x19[31:0] = dx19; x20[31:0] = dx20; x21[31:0] = dx21;
  //   x22[31:0] = dx22; x23[31:0] = dx23; x24[31:0] = dx24; x25[31:0] = dx25; x26[31:0] = dx26; x27[31:0] = dx27;
  //   x28[31:0] = dx28; x29[31:0] = dx29; x30[31:0] = dx30; x31[31:0] = dx31
endmodule
