// Logisim project smallacc.circ as structural Verilog: 2 circuits, main circuit main
module main (
  input  [31:0] X,
  output [31:0] Y
);

  wire clk_out;

  Clock clk (.out(clk_out));
  Register #(.width(32)) RegisterA ();  // open: D, en, clk, Q, clr
  Register #(.width(32)) RegisterB (.clk(clk_out));  // open: D, en, Q, clr
  signext signext_1 ();  // open: C, CX
  Adder #(.width(32)) adder_1 ();  // open: a, b, out, cin, cout
endmodule

module signext (
  input  [11:0] C,
  output [31:0] CX
);

  Multiplexer #(.width(21)) multiplexer_1 (.in0({21{1'b0}}), .in1({21{1'b0}}), .out(CX[31:11]), .sel(C[11]));

  assign CX[10:0] = C[10:0];
endmodule
